# Fritzing sketch Team 3 Circuit Digram  (saved by Fritzing 1.0.2b)
breadboards: 1

parts:
  Part1 = Arduino Uno (Rev3) - ICSP
  M1 = IR break beam 3mm rx [package=THT]
  M2 = IR break beam 3mm rx [package=THT]
  DFRobot_DFPlayer_Mini1 = DFRobot DFPlayer Mini [part_number=DFR0299]  # not connected
  R1 = Resistor [tolerance=±5% resistance=220 package="0805 [SMD]"]
  R2 = Resistor [tolerance=±5% resistance=220 package="0805 [SMD]"]
  LED1 = smd LED [color="Red (633nm)" package="0603 [SMD]"]
  J1 = Basic Servo
  R3 = Resistor [tolerance=±5% resistance=220 package="0805 [SMD]"]
  SP1 = SPEAKER [package=pcb_mount_speaker]  # not connected
  SP2 = SPEAKER [package=pcb_mount_speaker]  # not connected

nets:
  N1: Part1.D8, J1.pulse, R3.Pin_1
  N2: Part1.D9_PWM, R2.Pin_1, LED1.anode
  N3: Part1.D4, M1.pin2, R1.Pin_1
  5V: Part1.5V, M1.pin1, M2.pin1, J1.vcc
  GND: Part1.GND, M1.pin3, M2.pin3, LED1.cathode, J1.gnd

custom parts:
  IR break beam 3mm rx: Infrared break beam Sensor rx module.
